# Fritzing sketch wordclock v3 strip (saved by Fritzing 0.9.4)
circuit board: 42.137cm x 1.7671cm
breadboards: 1

parts:
  Pad1 = Pad [width=5 height=2 connect=center]
  Pad2 = Pad [width=5 height=2 connect=center]
  Pad3 = Pad [width=5 height=2 connect=center]
  Pad4 = Pad [width=5 height=2 connect=center]
  Pad5 = Pad [width=5 height=2 connect=center]
  Pad6 = Pad [width=5 height=2 connect=center]
  Pad7 = Pad [width=5 height=2 connect=center]
  Pad8 = Pad [width=5 height=2 connect=center]
  Pad9 = Pad [width=5 height=2 connect=center]  # not connected
  Pad10 = Pad [width=5 height=2 connect=center]
  Pad11 = Pad [width=5 height=2 connect=center]
  Pad12 = Pad [width=5 height=2 connect=center]
  Pad13 = Pad [width=5 height=2 connect=center]
  Pad14 = Pad [width=5 height=2 connect=center]
  Pad15 = Pad [width=5 height=2 connect=center]
  Pad16 = Pad [width=5 height=2 connect=center]
  Pad17 = Pad [width=5 height=2 connect=center]
  Pad18 = Pad [width=5 height=2 connect=center]
  Pad19 = Pad [width=5 height=2 connect=center]
  Pad20 = Pad [width=5 height=2 connect=center]
  Pad21 = Pad [width=5 height=2 connect=center]
  Pad22 = Pad [width=5 height=2 connect=center]
  Pad23 = Pad [width=5 height=2 connect=center]
  Pad24 = Pad [width=5 height=2 connect=center]
  Pad25 = Pad [width=5 height=2 connect=center]
  Pad26 = Pad [width=5 height=2 connect=center]
  Pad27 = Pad [width=5 height=2 connect=center]
  Pad28 = Pad [width=5 height=2 connect=center]
  Pad29 = Pad [width=5 height=2 connect=center]
  Pad30 = Pad [width=5 height=2 connect=center]
  Pad31 = Pad [width=5 height=2 connect=center]
  Pad32 = Pad [width=5 height=2 connect=center]
  Pad33 = Pad [width=5 height=2 connect=center]
  Pad34 = Pad [width=5 height=2 connect=center]
  Pad35 = Pad [width=5 height=2 connect=center]
  Pad36 = Pad [width=5 height=2 connect=center]
  Pad37 = Pad [width=5 height=2 connect=center]
  Pad38 = Pad [width=5 height=2 connect=center]
  Pad39 = Pad [width=5 height=2 connect=center]
  Pad40 = Pad [width=5 height=2 connect=center]
  Pad41 = Pad [width=5 height=2 connect=center]
  Pad42 = Pad [width=5 height=2 connect=center]
  Pad43 = Pad [width=5 height=2 connect=center]
  Pad44 = Pad [width=5 height=2 connect=center]
  Pad45 = Pad [width=5 height=2 connect=center]
  Pad46 = Pad [width=5 height=2 connect=center]
  Pad47 = Pad [width=5 height=2 connect=center]
  Pad48 = Pad [width=5 height=2 connect=center]
  Pad49 = Pad [width=5 height=2 connect=center]
  Pad50 = Pad [width=5 height=2 connect=center]
  Pad51 = Pad [width=5 height=2 connect=center]
  Pad52 = Pad [width=5 height=2 connect=center]
  Pad53 = Pad [width=5 height=2 connect=center]
  Pad54 = Pad [width=5 height=2 connect=center]
  Pad55 = Pad [width=5 height=2 connect=center]
  Pad56 = Pad [width=5 height=2 connect=center]
  Pad57 = Pad [width=5 height=2 connect=center]
  Pad58 = Pad [width=5 height=2 connect=center]
  Pad59 = Pad [width=5 height=2 connect=center]
  Pad60 = Pad [width=5 height=2 connect=center]
  Pad61 = Pad [width=5 height=2 connect=center]
  Pad62 = Pad [width=5 height=2 connect=center]
  Pad63 = Pad [width=5 height=2 connect=center]
  Pad64 = Pad [width=5 height=2 connect=center]
  Pad65 = Pad [width=5 height=2 connect=center]
  Pad66 = Pad [width=5 height=2 connect=center]
  Pad67 = Pad [width=5 height=2 connect=center]
  Pad68 = Pad [width=5 height=2 connect=center]
  Pad69 = Pad [width=5 height=2 connect=center]
  Pad70 = Pad [width=5 height=2 connect=center]
  Pad71 = Pad [width=5 height=2 connect=center]
  Pad72 = Pad [width=5 height=2 connect=center]
  Pad73 = Pad [width=5 height=2 connect=center]
  Pad74 = Pad [width=5 height=2 connect=center]
  Pad75 = Pad [width=5 height=2 connect=center]
  Pad76 = Pad [width=5 height=2 connect=center]
  Pad77 = Pad [width=5 height=2 connect=center]
  Pad78 = Pad [width=5 height=2 connect=center]
  Pad79 = Pad [width=5 height=2 connect=center]
  Pad80 = Pad [width=5 height=2 connect=center]
  Pad81 = Pad [width=5 height=2 connect=center]
  Pad82 = Pad [width=5 height=2 connect=center]
  Pad83 = Pad [width=5 height=2 connect=center]
  Pad84 = Pad [width=5 height=2 connect=center]
  Pad85 = Pad [width=5 height=2 connect=center]
  Pad86 = Pad [width=5 height=2 connect=center]
  Pad87 = Pad [width=5 height=2 connect=center]
  Pad88 = Pad [width=5 height=2 connect=center]
  Pad89 = Pad [width=5 height=2 connect=center]
  Pad90 = Pad [width=5 height=2 connect=center]
  Pad91 = Pad [width=5 height=2 connect=center]
  Pad92 = Pad [width=5 height=2 connect=center]
  Pad93 = Pad [width=5 height=2 connect=center]
  Pad94 = Pad [width=5 height=2 connect=center]
  Pad95 = Pad [width=5 height=2 connect=center]  # not connected
  Pad98 = Pad [width=5 height=2 connect=center]
  Pad99 = Pad [width=10 height=2 connect=center]
  Pad100 = Pad [width=10 height=2 connect=center]
  Pad101 = Pad [width=10 height=2 connect=center]
  Pad103 = Pad [width=10 height=2 connect=center]
  Pad104 = Pad [width=10 height=2 connect=center]

nets:
  N1: Pad1.pad, Pad4.pad
  N2: Pad2.pad, Pad5.pad
  N3: Pad3.pad, Pad6.pad
  N4: Pad7.pad, Pad99.pad
  N5: Pad8.pad, Pad100.pad
  N6: Pad10.pad, Pad15.pad
  N7: Pad11.pad, Pad12.pad
  N8: Pad13.pad, Pad14.pad
  N9: Pad16.pad, Pad21.pad
  N10: Pad17.pad, Pad18.pad
  N11: Pad19.pad, Pad20.pad
  N12: Pad22.pad, Pad27.pad
  N13: Pad23.pad, Pad24.pad
  N14: Pad25.pad, Pad26.pad
  N15: Pad28.pad, Pad33.pad
  N16: Pad29.pad, Pad30.pad
  N17: Pad31.pad, Pad32.pad
  N18: Pad34.pad, Pad39.pad
  N19: Pad35.pad, Pad36.pad
  N20: Pad37.pad, Pad38.pad
  N21: Pad40.pad, Pad45.pad
  N22: Pad41.pad, Pad42.pad
  N23: Pad43.pad, Pad44.pad
  N24: Pad46.pad, Pad51.pad
  N25: Pad47.pad, Pad48.pad
  N26: Pad49.pad, Pad50.pad
  N27: Pad52.pad, Pad57.pad
  N28: Pad53.pad, Pad54.pad
  N29: Pad55.pad, Pad56.pad
  N30: Pad58.pad, Pad63.pad
  N31: Pad59.pad, Pad60.pad
  N32: Pad61.pad, Pad62.pad
  N33: Pad64.pad, Pad69.pad
  N34: Pad65.pad, Pad66.pad
  N35: Pad67.pad, Pad68.pad
  N36: Pad70.pad, Pad75.pad
  N37: Pad71.pad, Pad72.pad
  N38: Pad73.pad, Pad74.pad
  N39: Pad76.pad, Pad81.pad
  N40: Pad77.pad, Pad78.pad
  N41: Pad79.pad, Pad80.pad
  N42: Pad82.pad, Pad85.pad
  N43: Pad83.pad, Pad86.pad
  N44: Pad84.pad, Pad87.pad
  N45: Pad88.pad, Pad93.pad
  N46: Pad89.pad, Pad90.pad
  N47: Pad91.pad, Pad92.pad
  N48: Pad94.pad, Pad104.pad
  N49: Pad98.pad, Pad101.pad, Pad103.pad

notes:
  --->
  -
  +
  Wordclock V3 G Bouma 2021
