# Fritzing sketch wordclock v5 esp32 (saved by Fritzing 0.9.4)
circuit board: 15.35cm x 3cm

parts:
  DS3231 = male pin header, 8 pins [form="♂ (male)"]
  Buzz- = male pin header, 1 pin [form="♂ (male)"]
  R1 = Resistor [tolerance=±5% resistance=330 package=THT]
  R2 = Resistor [tolerance=±5% resistance=330 package=THT]
  Buzz+ = male pin header, 1 pin [form="♂ (male)"]
  DO = female pin header, 1 pin [form="♀ (female)"]
  C1000 = Electrolytic Capacitor [capacitance=1000µF package="300 mil [THT, electrolytic]"]
  Power- = female pin header, 1 pin [form="♀ (female)"]
  - = male pin header, 1 pin [form="♂ (male)"]
  Led+ = male pin header, 1 pin [form="♂ (male)"]
  Power+ = female pin header, 1 pin [form="♀ (female)"]
  + = female pin header, 1 pin [form="♀ (female)"]
  BME260-6P = male pin header, 6 pins [form="♂ (male)"]
  HV = male pin header, 6 pins [form="♂ (male)"]
  LV = male pin header, 6 pins [form="♂ (male)"]
  Touch_0-3 = female pin header, 4 pins [form="♀ (female)"]
  Led- = male pin header, 1 pin [form="♂ (male)"]
  Vin = male pin header, 2 pins [form="♂ (male)"]
  Spare_I2C = male pin header, 4 pins [form="♂ (male)"]
  10uF_Cap = female pin header, 2 pins [form="♀ (female)"]
  R3 = Resistor [tolerance=±5% resistance=10k package=THT]
  LDR1 = Photocell (LDR) [package=THT]
  5V = female pin header, 19 pins [form="♀ (female)"]
  CLK = female pin header, 19 pins [form="♀ (female)"]

nets:
  N1: DS3231.pin1, BME260-6P.pin1, LV.pin4, Spare_I2C.pin1, LDR1.pin_0, 5V.pin19
  N2: DS3231.pin2, Buzz-.pin1, C1000.-, Power-.pin1, -.pin1, BME260-6P.pin2, HV.pin3, LV.pin3, Led-.pin1, Spare_I2C.pin2, 10uF_Cap.pin1, CLK.pin19
  N3: DS3231.pin3, BME260-6P.pin3, Spare_I2C.pin3, CLK.pin17
  N4: DS3231.pin4, BME260-6P.pin4, Spare_I2C.pin4, CLK.pin14
  N5: DS3231.pin7, CLK.pin8
  N6: R1.Pin_0, C1000.+, Power+.pin1, +.pin1, Vin.pin2
  N7: R1.Pin_1, Led+.pin1
  N8: R2.Pin_0, DO.pin1
  N9: R2.Pin_1, HV.pin6
  N10: Buzz+.pin1, HV.pin1
  N11: HV.pin4, Vin.pin1, 5V.pin1
  N12: LV.pin1, 5V.pin8
  N13: LV.pin6, 5V.pin7
  N14: Touch_0-3.pin1, CLK.pin7
  N15: Touch_0-3.pin2, CLK.pin6
  N16: Touch_0-3.pin3, CLK.pin5
  N17: Touch_0-3.pin4, CLK.pin4
  N18: 10uF_Cap.pin2, 5V.pin18
  N19: R3.Pin_0, 5V.pin6
  N20: R3.Pin_1, LDR1.pin_1, 5V.pin15

notes:
  Ledstrip
  power in
  Wordclock G Bouma V.5 ESP32
  Batterij boven!
  3.3v
  GND
  SDA
  SCL
  Level converter
  5v
  +
  38 pins / 23mm
