# Fritzing sketch wordclock v6.1 Mega (saved by Fritzing 0.9.4)
circuit board: 11.3315cm x 3.94439cm

parts:
  DS3231 = male pin header, 8 pins [form="♂ (male)"]
  R1 = Resistor [tolerance=±5% resistance=330 package=THT]
  R2 = Resistor [tolerance=±5% resistance=330 package=THT]
  DO = female pin header, 1 pin [form="♀ (female)"]
  C1000 = Electrolytic Capacitor [capacitance=1000µF package="300 mil [THT, electrolytic]"]
  Power- = female pin header, 1 pin [form="♀ (female)"]
  - = male pin header, 1 pin [form="♂ (male)"]
  Led+ = male pin header, 1 pin [form="♂ (male)"]
  Power+ = female pin header, 1 pin [form="♀ (female)"]
  + = female pin header, 1 pin [form="♀ (female)"]
  BME260-6P = male pin header, 6 pins [form="♂ (male)"]
  Led- = male pin header, 1 pin [form="♂ (male)"]
  WiFi = male pin header, 4 pins [form="♂ (male)"]
  M1 = Mega2560 R3 Pro ch340g

nets:
  N1: DS3231.pin1, BME260-6P.pin1, M1.3V3
  N2: DS3231.pin2, C1000.-, Power-.pin1, -.pin1, BME260-6P.pin2, Led-.pin1, WiFi.pin3, M1.GND
  N3: DS3231.pin3, BME260-6P.pin3, M1.21
  N4: DS3231.pin4, BME260-6P.pin4, M1.20
  N5: R1.Pin_0, C1000.+, Power+.pin1, +.pin1, WiFi.pin4, M1.VTG
  N6: R1.Pin_1, Led+.pin1
  N7: R2.Pin_0, DO.pin1
  N8: R2.Pin_1, M1.30
  N9: WiFi.pin1, M1.18
  N10: WiFi.pin2, M1.19

notes:
  Ledstrip
  power in
  Wordclock G Bouma V6.1 Mega
  Batterij boven!
  3.3v
  GND
  SDA
  SCL
  Vin
  Gnd
  Tx
  Rx

custom parts:
  Mega2560 R3 Pro ch340g: The Mega 2560 R3 Pro Mini :- Completely compatible with original Arduino Mega2560 Pin pitch: 0.1 inch Size: 5.42cm*3.68cm With Atmega16U2 chip as the USB to Serial converter 5V working voltage. Input Voltage:7-12V Analog Input Pins: 16 Digital I/O pins: 54 The Mega 2560 R3 Pro Mini has no datasheet and no info and I don't have one to compare, so I made this based on photos. Dec 2019 modified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
